# Fritzing sketch sketch02 (saved by Fritzing 0.9.3b)
breadboards: 1

parts:
  부품1 = Arduino Uno (Rev3)
  S1 = Pushbutton [package="[THT]"]
  R1 = Resistor [tolerance=±1% resistance=10k package=THT]  # not connected

nets:
  N1: 부품1.D3_PWM, S1.Pin_3, S1.Pin_4
  N2: 부품1.5V, S1.Pin_1, S1.Pin_2
