# Fritzing sketch sketch03 (saved by Fritzing 0.9.3b)
breadboards: 1

parts:
  부품1 = Arduino Uno (Rev3)
  J1 = Piezo Speaker
  U1 = POT [package=pot_alpha_rv16af-20]

nets:
  N1: 부품1.A0, U1.S
  N2: 부품1.GND, J1.pin1, U1.E
  N3: 부품1.D3_PWM, J1.pin2
  N4: 부품1.5V, U1.A
