# Fritzing sketch sketch06 (saved by Fritzing 0.9.3b)
breadboards: 1

parts:
  부품1 = Arduino Uno (Rev3)
  S1 = Momentary Switch [package=ksa_sealed_tac_switch]
  R1 = Resistor [tolerance=±5% resistance=330 package=THT]
  LED1 = LED - 5mm [color="Green (570nm)" package="5 mm [THT]"]
  R2 = Resistor [tolerance=±5% resistance=110 package="1206 [SMD]"]
  R3 = PHOTOCELL [package=photocell]
  R4 = Resistor [tolerance=±5% resistance=1k package="0402 [SMD]"]

nets:
  N1: 부품1.A0, R3.P$1, R4.Pin_1
  N2: 부품1.D2, S1.1, S1.2, R1.Pin_0
  N3: 부품1.D4, R2.Pin_0
  N4: 부품1.5V, S1.3, S1.4, R3.P$2
  N5: 부품1.GND, R1.Pin_1, LED1.cathode, R4.Pin_0
  N6: LED1.anode, R2.Pin_1
